// Digital circuit part_c.dig as structural Verilog
module part_c (
  input  in_0,
  input  in_1,
  input  in_2,
  output out_0
);

  wire fgnfet_1_s, fgnfet_4_s, pfet_1_d, pfet_2_d, pfet_3_d, pfet_4_d, pfet_6_d, pfet_7_d;

  PFET pfet_1 (.G(in_0), .S(1'b1), .D(pfet_1_d));
  NFET nfet_1 (.G(in_0), .D(pfet_1_d), .S(1'b0));
  PFET pfet_2 (.G(in_2), .S(1'b1), .D(pfet_2_d));
  NFET nfet_2 (.G(in_2), .D(pfet_2_d), .S(1'b0));
  PFET pfet_3 (.G(in_0), .S(1'b1), .D(pfet_3_d));
  NFET nfet_3 (.G(in_0), .D(pfet_3_d), .S(1'b0));
  PFET pfet_4 (.G(pfet_1_d), .S(1'b1), .D(pfet_4_d));
  PFET pfet_5 (.G(pfet_2_d), .S(pfet_4_d), .D(out_0));
  FGNFET fgnfet_1 (.G(in_2), .D(out_0), .S(fgnfet_1_s));
  PFET pfet_6 (.G(in_2), .S(1'b1), .D(pfet_6_d));
  NFET nfet_4 (.G(in_2), .D(pfet_6_d), .S(1'b0));
  FGNFET fgnfet_2 (.G(pfet_3_d), .D(fgnfet_1_s), .S(1'b0));
  FGNFET fgnfet_3 (.G(pfet_6_d), .D(fgnfet_1_s), .S(1'b0));
  PFET pfet_7 (.G(in_0), .S(1'b1), .D(pfet_7_d));
  PFET pfet_8 (.G(in_2), .S(pfet_7_d), .D(out_0));
  FGNFET fgnfet_4 (.G(in_0), .D(out_0), .S(fgnfet_4_s));
  FGNFET fgnfet_5 (.G(in_1), .D(fgnfet_4_s), .S(fgnfet_1_s));
  PFET pfet_9 (.G(in_1), .S(1'b1), .D(pfet_7_d));
endmodule

/* Test case part_c:
in_0 in_1 in_2 out_0
0    0    0    1
0    0    1    0
0    1    0    1
0    1    1    0
1    0    0    1
1    0    1    1
1    1    0    0
1    1    1    1
*/
