// Digital circuit lab2_part2.dig as structural Verilog
module lab2_part2 (
  input  in0,
  input  in1,
  input  in2,
  input  in3,
  output sign_a,
  output sign_f,
  output sign_b,
  output sign_g,
  output sign_e,
  output sign_c,
  output sign_d,
  output sign_dp,
  output seg_a,
  output seg_f,
  output seg_b,
  output seg_g,
  output seg_e,
  output seg_c,
  output seg_d,
  output seg_dp
);

  wire _0, _1, _2, _3, _4, _5, _6, _7, _8, decoder_1_out_1, decoder_1_out_2, decoder_1_out_3,
       decoder_1_out_4, decoder_1_out_5, decoder_1_out_6, decoder_1_out_7, decoder_1_out_9, decoder_1_out_10,
       decoder_1_out_11, decoder_1_out_12, decoder_1_out_13, decoder_1_out_14, decoder_1_out_15, or_8_out,
       or_9_out, or_10_out, or_11_out, or_12_out;

  Seven_Seg seven_seg_1 (.a(1'b0), .b(1'b0), .c(1'b0), .d(1'b0), .e(1'b0), .f(1'b0), .g(in3), .dp(1'b0));
  Seven_Seg seven_seg_2 (.a(seg_a), .b(seg_b), .c(seg_c), .d(seg_d), .e(seg_e), .f(seg_f), .g(seg_g), .dp(1'b0));
  or or_1 (seg_a, _8, _7, _6, _5, or_8_out);
  or or_2 (seg_b, _8, _7, _4, _3, or_9_out);
  or or_3 (seg_c, _8, _7, _6, _5, or_10_out);
  or or_4 (seg_d, _8, _6, _5, _3, or_11_out);
  or or_5 (seg_e, _8, _6, _2, _0);
  or or_6 (seg_f, _8, _6, _5, _4, _0);
  or or_7 (seg_g, _8, _6, _5, _4, or_12_out);
  or or_8 (or_8_out, _3, _2, _0);
  or or_9 (or_9_out, _2, _1, _0);
  or or_10 (or_10_out, _4, _3, _1, _0);
  or or_11 (or_11_out, _2, _0);
  or or_12 (or_12_out, _3, _2);
  Decoder #(.Selector_Bits(4)) decoder_1 (
    .sel({in3, in2, in1, in0}), .out_0(_0), .out_1(decoder_1_out_1), .out_2(decoder_1_out_2),
    .out_3(decoder_1_out_3), .out_4(decoder_1_out_4), .out_5(decoder_1_out_5), .out_6(decoder_1_out_6),
    .out_7(decoder_1_out_7), .out_8(_8), .out_9(decoder_1_out_9), .out_10(decoder_1_out_10),
    .out_11(decoder_1_out_11), .out_12(decoder_1_out_12), .out_13(decoder_1_out_13),
    .out_14(decoder_1_out_14), .out_15(decoder_1_out_15));
  or or_13 (_7, decoder_1_out_7, decoder_1_out_9);
  or or_14 (_6, decoder_1_out_6, decoder_1_out_10);
  or or_15 (_5, decoder_1_out_5, decoder_1_out_11);
  or or_16 (_4, decoder_1_out_4, decoder_1_out_12);
  or or_17 (_3, decoder_1_out_3, decoder_1_out_13);
  or or_18 (_2, decoder_1_out_2, decoder_1_out_14);
  or or_19 (_1, decoder_1_out_1, decoder_1_out_15);

  assign seg_dp = 1'b0;
  assign sign_a = 1'b0;
  assign sign_b = 1'b0;
  assign sign_c = 1'b0;
  assign sign_d = 1'b0;
  assign sign_dp = 1'b0;
  assign sign_e = 1'b0;
  assign sign_f = 1'b0;
  assign sign_g = in3;

  // Notes on the sheet:
  //   Interface (do not edit the content inside this box)
  //   Outputs:
  //   Inputs
  //   Sign
  //   Decimal Number
endmodule

/* Test case:
in3 in2 in1 in0  sign_a sign_b sign_c sign_d sign_e sign_f sign_g  seg_a seg_b seg_c seg_d seg_e seg_f seg_g
 0   0   0   0    0      0      0      0      0      0      0       1     1     1     1     1     1     0
*/
