// Digital circuit lab2_part3.dig as structural Verilog
module lab2_part3 (
  input  clk,
  input  in0,
  input  in1,
  input  in2,
  input  in3,
  input  sel_write_1,
  input  sel_write_0,
  input  sel_readA_1,
  input  sel_readA_0,
  input  sel_readB_1,
  input  sel_readB_0,
  output out0,
  output out1,
  output out2,
  output out3,
  output reg0_0,
  output reg0_1,
  output reg0_2,
  output reg0_3,
  output reg1_0,
  output reg1_1,
  output reg1_2,
  output reg1_3,
  output reg2_0,
  output reg2_1,
  output reg2_2,
  output reg2_3,
  output reg3_0,
  output reg3_1,
  output reg3_2,
  output reg3_3,
  output inA_0,
  output inA_1,
  output inA_2,
  output inA_3,
  output inB_0,
  output inB_1,
  output inB_2,
  output inB_3
);

  wire dig_0, dig_1, dig_2, dig_3, reg0_en, reg1_en, reg2_en, reg3_en;
  wire [3:0] reg0_in, reg_1_in, reg_2_in, reg_3_in;

  Demultiplexer #(.Bits(4), .Selector_Bits(2)) demultiplexer_1 (
    .sel({sel_write_1, sel_write_0}), .in({in3, in2, in1, in0}), .out_0(reg0_in), .out_1(reg_1_in),
    .out_2(reg_2_in), .out_3(reg_3_in));
  Decoder #(.Selector_Bits(2)) decoder_1 (
    .sel({sel_write_1, sel_write_0}), .out_0(reg0_en), .out_1(reg1_en), .out_2(reg2_en), .out_3(reg3_en));
  Register #(.Bits(4)) reg_0 (.D(reg0_in), .C(clk), .en(reg0_en), .Q({reg0_3, reg0_2, reg0_1, reg0_0}));
  Register #(.Bits(4)) reg_1 (.D(reg_1_in), .C(clk), .en(reg1_en), .Q({reg1_3, reg1_2, reg1_1, reg1_0}));
  Register #(.Bits(4)) reg_2 (.D(reg_2_in), .C(clk), .en(reg2_en), .Q({reg2_3, reg2_2, reg2_1, reg2_0}));
  Register #(.Bits(4)) reg_3 (.D(reg_3_in), .C(clk), .en(reg3_en), .Q({reg3_3, reg3_2, reg3_1, reg3_0}));
  Multiplexer #(.Selector_Bits(2)) multiplexer_1 (
    .sel({sel_readA_1, sel_readA_0}), .in_0(reg0_0), .in_1(reg1_0), .in_2(reg2_0), .in_3(reg3_0), .out(dig_0));
  Multiplexer #(.Selector_Bits(2)) multiplexer_2 (
    .sel({sel_readA_1, sel_readA_0}), .in_0(reg0_1), .in_1(reg1_1), .in_2(reg2_1), .in_3(reg3_1), .out(dig_1));
  Multiplexer #(.Selector_Bits(2)) multiplexer_3 (
    .sel({sel_readA_1, sel_readA_0}), .in_0(reg0_2), .in_1(reg1_2), .in_2(reg2_2), .in_3(reg3_2), .out(dig_2));
  Multiplexer #(.Selector_Bits(2)) multiplexer_4 (
    .sel({sel_readA_1, sel_readA_0}), .in_0(reg0_3), .in_1(reg1_3), .in_2(reg2_3), .in_3(reg3_3), .out(dig_3));
  Multiplexer #(.Selector_Bits(2)) multiplexer_5 (
    .sel({sel_readB_1, sel_readB_0}), .in_0(dig_0), .in_1(dig_3), .in_2(dig_2), .in_3(dig_1), .out(out0));
  Multiplexer #(.Selector_Bits(2)) multiplexer_6 (
    .sel({sel_readB_1, sel_readB_0}), .in_0(dig_1), .in_1(dig_0), .in_2(dig_3), .in_3(dig_2), .out(out1));
  Multiplexer #(.Selector_Bits(2)) multiplexer_7 (
    .sel({sel_readB_1, sel_readB_0}), .in_0(dig_2), .in_1(dig_1), .in_2(dig_0), .in_3(dig_3), .out(out2));
  Multiplexer #(.Selector_Bits(2)) multiplexer_8 (
    .sel({sel_readB_1, sel_readB_0}), .in_0(dig_3), .in_1(dig_2), .in_2(dig_1), .in_3(dig_0), .out(out3));
  Seven_Seg_Hex seven_seg_hex_1 (.d({2'b00, sel_readA_1, sel_readA_0}), .dp(1'b0));
  Seven_Seg_Hex seven_seg_hex_2 (.d({reg3_3, reg3_2, reg3_1, reg3_0}), .dp(1'b0));
  Seven_Seg_Hex seven_seg_hex_3 (.d({in3, in2, in1, in0}), .dp(1'b0));
  Seven_Seg_Hex seven_seg_hex_4 (.d({2'b00, sel_readB_1, sel_readB_0}), .dp(1'b0));
  Seven_Seg_Hex seven_seg_hex_5 (.d({reg2_3, reg2_2, reg2_1, reg2_0}), .dp(1'b0));
  Seven_Seg_Hex seven_seg_hex_6 (.d({2'b00, sel_write_1, sel_write_0}), .dp(1'b0));
  Seven_Seg_Hex seven_seg_hex_7 (.d({2'b00, sel_readA_1, sel_readA_0}), .dp(1'b0));
  Seven_Seg_Hex seven_seg_hex_8 (.d({out3, out2, out1, out0}), .dp(1'b0));
  Seven_Seg_Hex seven_seg_hex_9 (.d({reg1_3, reg1_2, reg1_1, reg1_0}), .dp(1'b0));
  Seven_Seg_Hex seven_seg_hex_10 (.d({2'b00, sel_readB_1, sel_readB_0}), .dp(1'b0));
  Seven_Seg_Hex seven_seg_hex_11 (.d({reg0_3, reg0_2, reg0_1, reg0_0}), .dp(1'b0));

  assign inA_0 = sel_readA_0;
  assign inA_1 = sel_readA_1;
  assign inA_2 = 1'b0;
  assign inA_3 = 1'b0;
  assign inB_0 = sel_readB_0;
  assign inB_1 = sel_readB_1;
  assign inB_2 = 1'b0;
  assign inB_3 = 1'b0;

  // Other names for the same wires on the sheet: rot_reg[1:0] = {sel_readA_1, sel_readA_0};
  //   rot_val[1:0] = {sel_readB_1, sel_readB_0}; write_reg[1:0] = {sel_write_1, sel_write_0}

  // Notes on the sheet:
  //   Which register to rotate
  //   Amount of left-hand rotation
  //   Which register to write to
  //   Digit 0
  //   Digit 1
  //   Digit 2
  //   Digit 3
  //   Interface (do not edit the content inside this box.You may however, right click on components to copy their label name)
  //   Inputs
  //   Keypad
  //   Outputs
  //   Registers
  //   Values read into ALU inputs
  //   Rotatee
  //   Register 3
  //   Synchronizing Clock
  //   Rotation amount:
  //   Register Selection: Write-to
  //   Register 2
  //   Register Selection: Read-from
  //   ALU Output
  //   ALU input A register address:
  //   Register 1
  //   ALU input B register address:
  //   Register 0
endmodule

/* Test case:
clk in3 in2 in1 in0 sel^write_1 sel^write_0 sel^readA_1 sel^readA_0 sel^readB_1 sel^readB_0  reg3_3 reg3_2 reg3_1 reg3_0 reg2_3 reg2_2 reg2_1 reg2_0 reg1_3 reg1_2 reg1_1 reg1_0 reg0_3 reg0_2 reg0_1 reg0_0 out3 out2 out1 out0
 0   0   0   0   0   0           0           0           0           0           0            0      0      0      0      0      0      0      0      0      0      0      0      0      0      0      0      0    0    0    0
 1   0   0   0   0   0           0           0           0           0           0            0      0      0      0      0      0      0      0      0      0      0      0      0      0      0      0      0    0    0    0
 0   0   1   0   1   1           1           0           0           0           0            0      0      0      0      0      0      0      0      0      0      0      0      0      0      0      0      0    0    0    0
 1   0   1   0   1   1           1           0           0           0           0            0      1      0      1      0      0      0      0      0      0      0      0      0      0      0      0      0    0    0    0
 0   0   0   0   1   0           1           0           0           0           0            0      1      0      1      0      0      0      0      0      0      0      0      0      0      0      0      0    0    0    0
 1   0   0   0   1   0           1           0           0           0           0            0      1      0      1      0      0      0      0      0      0      0      1      0      0      0      0      0    0    0    0
 0   0   0   0   0   0           0           1           1           0           1            0      1      0      1      0      0      0      0      0      0      0      1      0      0      0      0      1    0    1    0
 1   0   0   0   0   0           0           1           1           0           1            0      1      0      1      0      0      0      0      0      0      0      1      0      0      0      0      1    0    1    0
 0   0   0   0   0   0           0           0           1           1           1            0      1      0      1      0      0      0      0      0      0      0      1      0      0      0      0      1    0    0    0
 1   0   0   0   0   0           0           0           1           1           1            0      1      0      1      0      0      0      0      0      0      0      1      0      0      0      0      1    0    0    0
*/
