// Digital circuit playWithTunnels.dig as structural Verilog
module playWithTunnels (
  input  in_0,
  input  in_1,
  input  in_2,
  input  in_3,
  input  s_0,
  input  s_1,
  output out_0
);

  Multiplexer #(.Selector_Bits(2)) multiplexer_1 (
    .sel({s_1, s_0}), .in_0(in_0), .in_1(in_1), .in_2(in_2), .in_3(in_3), .out(out_0));

  // Notes on the sheet:
  //   Note how both the 2 tunnels in the circuit have the same name "wire1". 
  //   This signifies electrical connectivity
endmodule
